// Logisim project Logigrama - Trabalho Prático.circ as structural Verilog: 3 circuits, main circuit main
module main (
  input  BI,
  input  SNA,
  input  STA,
  output MD,
  output ME,
  output MC,
  output BA,
  output RAQ,
  output VA
);

  wire and_1_out, and_2_out, and_3_out, clock_1_out, d_ff_1_q, d_ff_1_qn,
       \módulo_de_controle_da_lavagem_1_lc , \módulo_de_controle_da_água_1_fim , not_1_out, or_1_out;

  Clock clock_1 (.out(clock_1_out));
  and and_1 (and_1_out, BI, d_ff_1_qn);
  not not_1 (not_1_out, \módulo_de_controle_da_lavagem_1_lc );
  or or_1 (or_1_out, d_ff_1_q, and_1_out);
  and and_2 (and_2_out, not_1_out, or_1_out);
  D_Flip_Flop d_ff_1 (.clk(clock_1_out), .D(and_2_out), .Q(d_ff_1_q), .Qn(d_ff_1_qn));  // open: preset, en, reset
  and and_3 (and_3_out, BI, d_ff_1_qn);
  \Módulo_de_Controle_da_Água  \módulo_de_controle_da_água_1  (
    .BI(and_3_out), .SNA(SNA), .STA(STA), .VA(VA), .RAQ(RAQ), .FIM(\módulo_de_controle_da_água_1_fim ));
  \Módulo_de_Controle_da_Lavagem  \módulo_de_controle_da_lavagem_1  (
    .RAQ(\módulo_de_controle_da_água_1_fim ), .SNA(SNA), .MD(MD), .MC(MC),
    .LC(\módulo_de_controle_da_lavagem_1_lc ), .ME(ME), .BA(BA));
endmodule

module \Módulo_de_Controle_da_Água  (
  input  BI,
  input  SNA,
  input  STA,
  output VA,
  output RAQ,
  output FIM
);

  wire and_1_out, and_2_out, and_3_out, and_4_out, clock_1_out, not_1_out, not_2_out, not_3_out, not_4_out,
       or_1_out, or_2_out, t_ff_1_q, t_ff_2_q;

  Clock clock_1 (.out(clock_1_out));
  and and_1 (and_1_out, t_ff_1_q, SNA);
  and and_2 (and_2_out, t_ff_1_q, t_ff_2_q);
  and and_3 (and_3_out, STA, t_ff_2_q);
  not not_1 (not_1_out, t_ff_2_q);
  not not_2 (not_2_out, t_ff_1_q);
  and and_4 (and_4_out, BI, not_1_out, not_2_out);
  or or_1 (or_1_out, and_1_out, and_2_out, and_3_out, and_4_out);
  or or_2 (or_2_out, and_1_out, and_2_out);
  T_Flip_Flop t_ff_1 (.clk(clock_1_out), .T(or_1_out), .Q(t_ff_1_q));  // open: Qn, preset, reset, en
  T_Flip_Flop t_ff_2 (.clk(clock_1_out), .T(or_2_out), .Q(t_ff_2_q));  // open: Qn, preset, reset, en
  not not_3 (not_3_out, t_ff_2_q);
  not not_4 (not_4_out, t_ff_1_q);
  and and_5 (VA, t_ff_1_q, not_3_out);
  and and_6 (RAQ, not_4_out, t_ff_2_q);
  and and_7 (FIM, t_ff_1_q, t_ff_2_q);

  // Notes on the sheet:
  //   T0
  //   T1
endmodule

module \Módulo_de_Controle_da_Lavagem  (
  input  RAQ,
  input  SNA,
  output MD,
  output MC,
  output LC,
  output ME,
  output BA
);

  wire and_1_out, and_2_out, and_3_out, and_4_out, and_5_out, and_6_out, and_7_out, and_8_out, and_9_out,
       and_10_out, and_11_out, and_12_out, and_13_out, and_14_out, and_15_out, and_16_out, clock_1_out, D0_q,
       D0_qn, D1_q, D1_qn, D2_q, D2_qn, not_1_out, or_1_out, or_3_out, or_6_out;

  Clock clock_1 (.out(clock_1_out));
  or or_1 (or_1_out, and_4_out, and_3_out, and_2_out, and_1_out);
  D_Flip_Flop D0 (.clk(clock_1_out), .D(or_1_out), .Q(D0_q), .Qn(D0_qn));  // open: preset, en, reset
  and and_1 (and_1_out, D0_qn, RAQ);
  and and_2 (and_2_out, D1_q, D0_qn);
  and and_3 (and_3_out, D2_q, D0_qn);
  and and_4 (and_4_out, D2_q, D1_qn, SNA);
  and and_5 (and_5_out, D2_qn, D0_qn, D1_q);
  not not_1 (not_1_out, SNA);
  and and_6 (and_6_out, D0_q, D1_qn, D2_qn);
  or or_2 (MD, and_5_out, and_6_out);
  and and_7 (and_7_out, D0_q, D2_qn, D1_qn);
  and and_8 (and_8_out, D1_q, D0_qn);
  and and_9 (and_9_out, D0_q, D1_qn, not_1_out);
  and and_10 (and_10_out, D0_q, D1_q, D2_qn);
  or or_3 (or_3_out, and_7_out, and_8_out, and_9_out);
  and and_11 (and_11_out, D0_qn, D1_qn, D2_q);
  or or_4 (ME, and_10_out, and_11_out);
  D_Flip_Flop D1 (.clk(clock_1_out), .D(or_3_out), .Q(D1_q), .Qn(D1_qn));  // open: preset, en, reset
  and and_12 (and_12_out, D0_qn, D1_q, D2_q);
  or or_5 (BA, and_12_out, and_13_out);
  and and_13 (and_13_out, D0_q, D1_qn, D2_q);
  and and_14 (and_14_out, D2_q, D1_qn);
  and and_15 (and_15_out, D0_q, D1_q, D2_qn);
  and and_16 (and_16_out, D2_q, D0_qn);
  and and_17 (MC, D0_qn, D1_q, D2_q);
  D_Flip_Flop D2 (.clk(clock_1_out), .D(or_6_out), .Q(D2_q), .Qn(D2_qn));  // open: preset, en, reset
  or or_6 (or_6_out, and_14_out, and_15_out, and_16_out);
  and and_18 (LC, D0_q, D1_q, D2_q);
endmodule
