// Logisim project Módulo de Controle da Lavagem.circ as structural Verilog: 1 circuit, main circuit main
module main (
  input  SNA,
  output MD,
  output ME,
  output MC,
  output BA
);

  wire and_1_out, and_2_out, and_3_out, and_4_out, and_5_out, and_6_out, and_7_out, and_8_out, and_9_out,
       and_10_out, and_11_out, and_12_out, and_13_out, and_14_out, and_15_out, and_17_out, and_18_out,
       and_20_out, and_21_out, clock_1_out, not_1_out, not_2_out, not_3_out, not_4_out, not_5_out, not_6_out,
       not_7_out, not_8_out, not_9_out, or_1_out, or_2_out, or_3_out, or_4_out, t_ff_1_q, t_ff_2_q, t_ff_3_q,
       t_ff_4_q;

  not not_1 (not_1_out, t_ff_2_q);
  not not_2 (not_2_out, SNA);
  not not_3 (not_3_out, t_ff_3_q);
  not not_4 (not_4_out, t_ff_4_q);
  not not_5 (not_5_out, t_ff_1_q);
  and and_1 (and_1_out, t_ff_1_q, t_ff_3_q);
  and and_2 (and_2_out, t_ff_2_q, t_ff_3_q, t_ff_4_q);
  and and_3 (and_3_out, SNA, not_1_out, t_ff_3_q, t_ff_4_q);
  and and_4 (and_4_out, t_ff_3_q, t_ff_4_q, not_2_out);
  and and_5 (and_5_out, not_1_out, t_ff_4_q, SNA);
  and and_6 (and_6_out, not_3_out, t_ff_4_q, SNA);
  and and_7 (and_7_out, not_2_out, t_ff_4_q);
  and and_8 (and_8_out, not_2_out, t_ff_1_q, t_ff_3_q);
  and and_9 (and_9_out, t_ff_1_q, not_3_out);
  and and_10 (and_10_out, not_3_out, not_4_out);
  and and_11 (and_11_out, not_5_out, not_1_out);
  and and_12 (and_12_out, t_ff_1_q, t_ff_2_q);
  and and_13 (and_13_out, t_ff_1_q, t_ff_4_q);
  and and_14 (and_14_out, not_5_out, t_ff_2_q, not_4_out, SNA);
  and and_15 (and_15_out, not_5_out, t_ff_3_q);
  or or_1 (or_1_out, and_1_out, and_2_out);
  or or_2 (or_2_out, and_3_out, and_4_out);
  or or_3 (or_3_out, and_5_out, and_6_out, and_7_out, and_8_out);
  or or_4 (or_4_out, and_9_out, and_10_out, and_11_out, and_12_out, and_13_out, and_14_out, and_15_out);
  Clock clock_1 (.out(clock_1_out));
  T_Flip_Flop t_ff_1 (.clk(clock_1_out), .T(or_1_out), .Q(t_ff_1_q));  // open: Qn, preset, reset, en
  T_Flip_Flop t_ff_2 (.clk(clock_1_out), .T(or_2_out), .Q(t_ff_2_q));  // open: Qn, preset, reset, en
  T_Flip_Flop t_ff_3 (.clk(clock_1_out), .T(or_3_out), .Q(t_ff_3_q));  // open: Qn, preset, reset, en
  T_Flip_Flop t_ff_4 (.clk(clock_1_out), .T(or_4_out), .Q(t_ff_4_q));  // open: Qn, preset, reset, en
  not not_6 (not_6_out, t_ff_1_q);
  not not_7 (not_7_out, t_ff_2_q);
  not not_8 (not_8_out, t_ff_3_q);
  not not_9 (not_9_out, t_ff_4_q);
  and and_16 (MD, not_6_out, not_7_out, not_8_out);
  and and_17 (and_17_out, t_ff_2_q, not_8_out, not_9_out);
  and and_18 (and_18_out, not_7_out, t_ff_3_q, t_ff_4_q);
  and and_19 (MC, not_9_out, not_8_out, t_ff_1_q);
  and and_20 (and_20_out, t_ff_1_q, not_8_out, not_9_out);
  and and_21 (and_21_out, t_ff_2_q, t_ff_3_q, t_ff_4_q);
  or or_5 (ME, and_17_out, and_18_out);
  or or_6 (BA, and_20_out, and_21_out);

  // Notes on the sheet:
  //   T3
  //   T2
  //   T1
  //   T0
endmodule
