// Logisim project Módulo de Controle da Água.circ as structural Verilog: 1 circuit, main circuit main
module main (
  input  BI,
  input  SNA,
  input  STA,
  output VA,
  output RAQ
);

  wire and_1_out, and_2_out, and_3_out, and_4_out, clock_1_out, not_1_out, not_2_out, not_3_out, not_4_out,
       or_1_out, or_2_out, t_ff_1_q, t_ff_2_q;

  Clock clock_1 (.out(clock_1_out));
  not not_1 (not_1_out, t_ff_2_q);
  not not_2 (not_2_out, t_ff_1_q);
  and and_1 (and_1_out, t_ff_1_q, SNA);
  and and_2 (and_2_out, t_ff_1_q, t_ff_2_q);
  and and_3 (and_3_out, STA, t_ff_2_q);
  and and_4 (and_4_out, BI, not_1_out, not_2_out);
  or or_1 (or_1_out, and_1_out, and_2_out, and_3_out, and_4_out);
  or or_2 (or_2_out, and_1_out, and_2_out);
  T_Flip_Flop t_ff_1 (.clk(clock_1_out), .T(or_1_out), .Q(t_ff_1_q));  // open: Qn, preset, reset, en
  T_Flip_Flop t_ff_2 (.clk(clock_1_out), .T(or_2_out), .Q(t_ff_2_q));  // open: Qn, preset, reset, en
  not not_3 (not_3_out, t_ff_2_q);
  not not_4 (not_4_out, t_ff_1_q);
  and and_5 (VA, t_ff_1_q, not_3_out);
  and and_6 (RAQ, not_4_out, t_ff_2_q);

  // Notes on the sheet:
  //   T0
  //   T1
endmodule
